# Fritzing sketch Untitled Sketch (saved by Fritzing 0.9.3b)
breadboards: 1

parts:
  IC1 = L293D [package=THT]
  Componente1 = Arduino Uno (Rev3) - ICSP
  Componente2 = Bluetooth HC-05 Macho
  J1 = Piezo Speaker  # not connected
  M1 = DC Motor
  M2 = DC Motor
  hc-sr1 = hc-sr04

nets:
  N1: IC1.Enable_1, Componente1.D10_PWM/SS
  N2: IC1.In_1, Componente1.D6_PWM
  N3: IC1.Out_1_(_Controlled_by_Enable_1_), M1.pin_1, M1.pin_2
  GND: IC1.0V, Componente1.GND, Componente2.GND, hc-sr1.GND
  N4: IC1.In_2, Componente1.D7
  N5: IC1.+Vmotor, Componente1.VIN
  N6: IC1.Enable_2, Componente1.D11_PWM/MOSI
  N7: IC1.In_3, Componente1.D8
  N8: IC1.Out_3_(_Controlled_by_Enable_2_), M2.pin_2
  N9: IC1.Out_4_(_Controlled_by_Enable_2_), M2.pin_1
  N10: IC1.In_4, Componente1.D9_PWM
  N11: IC1.+V, Componente1.5V
  N12: Componente1.D0/RX, Componente2.TXD
  N13: Componente1.D1/TX, Componente2.RXD
  N14: Componente1.D3_PWM, hc-sr1.Echo
  N15: Componente1.D5_PWM, hc-sr1.Trig
